# Fritzing sketch FallAnalyzerShield (saved by Fritzing 0.9.3b)
circuit board: 8.46667cm x 5.64444cm
breadboards: 1

parts:
  Part1 = Arduino Uno (Rev3)
  Accelerometer = Camdenboss CTB0158-5 [part_number=CTB0158-5 package=THT]
  MicroSD_Module = MicroSD Card Module
  R2 = Resistor [tolerance=±5% resistance=220 package="0402 [SMD]"]
  R1 = Resistor [tolerance=±5% resistance=220 package="0402 [SMD]"]
  Device_Ready = Camdenboss CTB0158-2 [part_number=CTB0158-2 package=THT]
  GPS_Connection = Camdenboss CTB0158-2 [part_number=CTB0158-2 package=THT]
  Buzzer = Camdenboss CTB0158-2 [part_number=CTB0158-2 package=THT]
  False_Alarm_Button = Camdenboss CTB0158-2 [part_number=CTB0158-2 package=THT]

nets:
  N1: Part1.A0, Buzzer.pin2
  N2: Part1.A1, Device_Ready.pin2
  N3: Part1.A2, GPS_Connection.pin2
  N4: Part1.A3, False_Alarm_Button.pin2
  N5: Part1.A4/SDA, Accelerometer.pin4
  N6: Part1.A5/SCL, Accelerometer.pin3
  N7: Part1.D11_PWM/MOSI, MicroSD_Module.MOSI
  N8: Part1.D12/MISO, MicroSD_Module.GND
  N9: Part1.D13/SCK, MicroSD_Module.VCC
  N10: Part1.GND, Accelerometer.pin2, MicroSD_Module.SCK, R2.Pin_0, R1.Pin_0, Buzzer.pin1, False_Alarm_Button.pin1
  N11: Part1.D2, Accelerometer.pin5
  N12: Part1.D4, MicroSD_Module.MISO
  N13: Part1.5V, Accelerometer.pin1, MicroSD_Module.CS
  N14: R2.Pin_1, Device_Ready.pin1
  N15: R1.Pin_1, GPS_Connection.pin1
